// Logisim project circuit.circ as structural Verilog: 1 circuit, main circuit main
module main (
  input  A,
  input  B,
  input  C,
  input  D,
  output IMPAR_ODD
);

  wire buffer_1_out, nand_1_out, nand_2_out, nand_3_out, nand_4_out, nand_5_out, nand_6_out, nand_7_out,
       nand_8_out;

  nand nand_1 (nand_1_out, A, B);
  buf buffer_1 (buffer_1_out, nand_1_out);
  nand nand_2 (nand_2_out, C, D);
  nand nand_3 (nand_3_out, C, nand_2_out);
  nand nand_4 (nand_4_out, nand_2_out, D);
  nand nand_5 (nand_5_out, A, buffer_1_out);
  nand nand_6 (nand_6_out, buffer_1_out, B);
  nand nand_7 (nand_7_out, nand_3_out, nand_4_out);
  nand nand_8 (nand_8_out, nand_5_out, nand_6_out);
  xor xor_1 (IMPAR_ODD, nand_8_out, nand_7_out);

  // Notes on the sheet:
  //   TTL
  //   DTL
  //   SN74HC86N
endmodule
